# Fritzing sketch esquema (saved by Fritzing 0.9.3b)
breadboards: 1

parts:
  R1 = Resistor [tolerance=±5% resistance=220 package=THT]
  R2 = Resistor [tolerance=±5% resistance=220 package=THT]
  LED1 = LED - 5mm [color="Red (633nm)" package="5 mm [THT]"]
  LED2 = LED - 5mm [color="Green (570nm)" package="5 mm [THT]"]
  LCM1602_IIC1 = LCM1602 IIC [part_number="LCM1602 IIC" chip_label="LCM1602 IIC" package="DIP (Dual Inline) [THT]"]
  LCD1 = LCD screen
  YwRobot_Power_Supply1 = YwRobot Breadboard Power Supply [part_number=545043]
  RHT1 = Humidity and Temperature Sensor RHT03
  Mod1 = KY-019 5V Relay Module [package="Breakout board"]
  Power_plug1 = Power plug
  LED4 = LEDs [package=led10mm]
  U1 = ESP8266 NodeMCU LoLin module

nets:
  N1: R1.Pin_0, LED1.anode
  N2: R1.Pin_1, U1.D4
  N3: R2.Pin_0, LED2.anode
  N4: R2.Pin_1, U1.D5
  N5: LED1.cathode, LED2.cathode, LCM1602_IIC1.GND, YwRobot_Power_Supply1.GND#11, YwRobot_Power_Supply1.GND#12
  VSS: LCM1602_IIC1.VSS, LCD1.VSS
  VDD: LCM1602_IIC1.VDD, LCD1.VDD
  N6: LCM1602_IIC1.V0, LCD1.V0
  N7: LCM1602_IIC1.RS, LCD1.RS
  N8: LCM1602_IIC1.RW, LCD1.R/W
  N9: LCM1602_IIC1.E, LCD1.E
  N10: LCM1602_IIC1.D0, LCD1.DB0
  N11: LCM1602_IIC1.D1, LCD1.DB1
  N12: LCM1602_IIC1.D2, LCD1.DB2
  N13: LCM1602_IIC1.D3, LCD1.DB3
  N14: LCM1602_IIC1.D4, LCD1.DB4
  N15: LCM1602_IIC1.D5, LCD1.DB5
  N16: LCM1602_IIC1.D6, LCD1.DB6
  N17: LCM1602_IIC1.D7, LCD1.DB7
  N18: LCM1602_IIC1.A, LCD1.LED+
  N19: LCM1602_IIC1.K, LCD1.LED-
  N20: LCM1602_IIC1.VCC, YwRobot_Power_Supply1.VCC#5, YwRobot_Power_Supply1.VCC#6
  N21: LCM1602_IIC1.SDA, U1.D2
  N22: LCM1602_IIC1.SCL, U1.D1
  N23: YwRobot_Power_Supply1.VCC#9, YwRobot_Power_Supply1.VCC#10, RHT1.Vcc, Mod1.+
  N24: YwRobot_Power_Supply1.GND#13, YwRobot_Power_Supply1.GND#14, RHT1.GND_2, Mod1.-
  N25: RHT1.GND_1, U1.D6
  N26: Mod1.S, U1.D7
  N27: Mod1.Common, Power_plug1.GND
  N28: Mod1.NO, LED4.C
  N29: Power_plug1.VCC, LED4.A

custom parts:
  LCM1602 IIC: I2C-Module to use a 1602 or 2004 LCD on with the wire.h libory Serial LCD Modul
  YwRobot Breadboard Power Supply: The YwRobot Breadboard Power Supply (MB-V2) has two power rails; they can be 5V or 3V3. Power to the module can be provided through the female USB socket or through the A10 (female) 2.1mm power jack.
  KY-019 5V Relay Module: KY-019 5V Relay module, used to control AC circuits. (Special thanks to vanepp for fixing the PCB holes and other errors)
  LEDs: LEDs Standard schematic elements and footprints for 5mm, 3mm, 1206, and 0603 sized LEDs. 5mm - Spark Fun Electronics SKU : COM-00529 (and others)
  ESP8266 NodeMCU LoLin module: ESP8266 based NodeMCU
